// Logisim project lab04.circ as structural Verilog: 13 circuits, main circuit main
module main (
);

  wire alucontrolcircuit_1_alu_src, and_1_out, clock_1_out, comparator_1_eq, control_1_branch,
       control_1_memread, control_1_memtoreg, control_1_memwrite, control_1_regwrite;
  wire [3:0] alucontrolcircuit_1_alu_ctrl0;
  wire [7:0] register_1_q_2;
  wire [23:0] register_1_q;
  wire [31:0] adder_1_out, adder_2_out, datamemory_1_readdata, immgen_1_out_2,
       instructionmemory_1_instruction, multiplexer_1_out, multiplexer_2_out, multiplexer_3_out,
       registerfilelong_1_rdata1, registerfilelong_1_rdata2, thirtytwobitalu_1_result;

  Register #(.width(32)) register_1 (
    .D(multiplexer_2_out), .en(1'b1), .clk(clock_1_out), .Q({register_1_q_2, register_1_q}));  // open: clr
  Adder #(.width(32)) adder_1 (.a({register_1_q_2, register_1_q}), .b(32'h4), .out(adder_1_out));  // open: cin, cout
  Clock clock_1 (.out(clock_1_out));
  InstructionMemory instructionmemory_1 (
    .Address(register_1_q), .ClockIn(clock_1_out), .Instruction(instructionmemory_1_instruction));
  ImmGen immgen_1 (.Instruction(instructionmemory_1_instruction), .out_2(immgen_1_out_2));
  Control control_1 (
    .l6(instructionmemory_1_instruction[6]), .l5(instructionmemory_1_instruction[5]),
    .l4(instructionmemory_1_instruction[4]), .l3(instructionmemory_1_instruction[3]),
    .l2(instructionmemory_1_instruction[2]), .l1(instructionmemory_1_instruction[1]),
    .l0(instructionmemory_1_instruction[0]), .MemToReg(control_1_memtoreg), .RegWrite(control_1_regwrite),
    .MemRead(control_1_memread), .MemWrite(control_1_memwrite), .Branch(control_1_branch));
  RegisterFileLong registerfilelong_1 (
    .RReg1(instructionmemory_1_instruction[19:15]), .RReg2(instructionmemory_1_instruction[24:20]),
    .WData(multiplexer_3_out), .Clock_in(clock_1_out), .Write(control_1_regwrite),
    .WReg(instructionmemory_1_instruction[11:7]), .RData1(registerfilelong_1_rdata1),
    .RData2(registerfilelong_1_rdata2));
  AluControlCircuit alucontrolcircuit_1 (
    .l30(instructionmemory_1_instruction[30]), .l14(instructionmemory_1_instruction[14]),
    .l13(instructionmemory_1_instruction[13]), .l12(instructionmemory_1_instruction[12]),
    .l6(instructionmemory_1_instruction[6]), .l5(instructionmemory_1_instruction[5]),
    .l4(instructionmemory_1_instruction[4]), .alu_ctrl3(alucontrolcircuit_1_alu_ctrl0[3]),
    .alu_ctrl2(alucontrolcircuit_1_alu_ctrl0[2]), .alu_ctrl1(alucontrolcircuit_1_alu_ctrl0[1]),
    .alu_ctrl0(alucontrolcircuit_1_alu_ctrl0[0]), .alu_src(alucontrolcircuit_1_alu_src));
  Multiplexer #(.enable("false"), .width(32)) multiplexer_1 (
    .in0(registerfilelong_1_rdata2), .in1(immgen_1_out_2), .out(multiplexer_1_out),
    .sel(alucontrolcircuit_1_alu_src));
  Comparator #(.width(32)) comparator_1 (
    .a(registerfilelong_1_rdata1), .b(registerfilelong_1_rdata2), .eq(comparator_1_eq));  // open: gt, lt
  ThirtyTwoBitAlu thirtytwobitalu_1 (
    .ALU_ctrl(alucontrolcircuit_1_alu_ctrl0), .A(registerfilelong_1_rdata1), .B(multiplexer_1_out),
    .Result(thirtytwobitalu_1_result));  // open: C_out
  Adder #(.width(32)) adder_2 (
    .a({register_1_q_2, register_1_q}), .b(immgen_1_out_2), .out(adder_2_out));  // open: cin, cout
  and and_1 (and_1_out, control_1_branch, comparator_1_eq);
  Multiplexer #(.enable("false"), .width(32)) multiplexer_2 (
    .in0(adder_1_out), .in1(adder_2_out), .out(multiplexer_2_out), .sel(and_1_out));
  DataMemory datamemory_1 (
    .Address(thirtytwobitalu_1_result[25:0]), .MemWrite(control_1_memwrite), .MemRead(control_1_memread),
    .ClockIn(clock_1_out), .WriteData(registerfilelong_1_rdata2), .ReadData(datamemory_1_readdata));
  Multiplexer #(.enable("false"), .width(32)) multiplexer_3 (
    .in0(thirtytwobitalu_1_result), .in1(datamemory_1_readdata), .out(multiplexer_3_out),
    .sel(control_1_memtoreg));
endmodule

module ImmGen (
  input  [31:0] Instruction,
  output [31:0] out_2
);

  assign out_2[31:12] = {{19{Instruction[31]}}, Instruction[31]};  // Bit_Extender bit_extender_1
  Multiplexer #(.enable("false"), .select(2)) multiplexer_1 (
    .in0(Instruction[20]), .in1(Instruction[7]), .in3(1'b0), .out(out_2[0]), .sel(Instruction[6:5]));  // open: in2
  Multiplexer #(.enable("false"), .width(4)) multiplexer_2 (
    .in0(Instruction[24:21]), .in1(Instruction[11:8]), .out(out_2[4:1]), .sel(Instruction[5]));
  Multiplexer #(.enable("false")) multiplexer_3 (
    .in0(Instruction[31]), .in1(Instruction[7]), .out(out_2[11]), .sel(Instruction[6]));

  assign out_2[10:5] = Instruction[30:25];

  // Other names for the same wires on the sheet: l5 = Instruction[5]; l6_5[1:0] = Instruction[6:5];
  //   l6 = Instruction[6]; l7 = Instruction[7]; l11_8[3:0] = Instruction[11:8]; l_20 = Instruction[20];
  //   l24_21[3:0] = Instruction[24:21]; l31 = Instruction[31]; l30_25[5:0] = Instruction[30:25]
endmodule

module Control (
  input  l6,
  input  l5,
  input  l4,
  input  l3,
  input  l2,
  input  l1,
  input  l0,
  output MemToReg,
  output RegWrite,
  output MemRead,
  output MemWrite,
  output Branch
);

  wire not_1_out, not_2_out;

  not not_1 (not_1_out, l6);
  not not_2 (not_2_out, l5);
  not not_3 (MemToReg, l4);
  or or_1 (RegWrite, not_2_out, l4);
  and and_1 (MemRead, not_2_out, MemToReg);
  and and_2 (MemWrite, not_1_out, l5, MemToReg);

  assign Branch = l6;
endmodule

module InstructionMemory (
  input  [23:0] Address,
  input  ClockIn,
  output [31:0] Instruction
);

  wire not_1_out;

  not not_1 (not_1_out, ClockIn);
  RAM #(.addrWidth(22), .asyncread("true"), .dataWidth(32)) ram_1 (
    .addr(Address[23:2]), .we(1'b0), .oe(not_1_out), .dout(Instruction));  // open: clk, din
endmodule

module DataMemory (
  input  [25:0] Address,
  input  MemWrite,
  input  MemRead,
  input  ClockIn,
  input  [31:0] WriteData,
  output [31:0] ReadData
);

  RAM #(.addrWidth(24), .asyncread("true"), .dataWidth(32)) ram_1 (
    .addr(Address[25:2]), .we(MemWrite), .oe(MemRead), .clk(ClockIn), .din(WriteData), .dout(ReadData));
endmodule

module AluControlCircuit (
  input  l30,
  input  l14,
  input  l13,
  input  l12,
  input  l6,
  input  l5,
  input  l4,
  output alu_ctrl3,
  output alu_ctrl2,
  output alu_ctrl1,
  output alu_ctrl0,
  output alu_src
);

  wire and_1_out, and_2_out, and_3_out, and_4_out, and_5_out, and_6_out, not_1_out, not_2_out, not_3_out,
       not_4_out, not_5_out, not_6_out;

  not not_1 (not_1_out, l14);
  not not_2 (not_2_out, l13);
  not not_3 (not_3_out, l12);
  not not_4 (not_4_out, l6);
  not not_5 (not_5_out, l5);
  not not_6 (not_6_out, l4);
  and and_1 (and_1_out, l30, not_1_out, not_2_out, l5);
  and and_2 (and_2_out, l30, not_1_out, l5, l4);
  and and_3 (and_3_out, l30, not_1_out, l6, l5);
  and and_4 (and_4_out, l30, not_1_out, l12, l5);
  and and_5 (and_5_out, not_1_out, not_3_out, not_4_out, not_6_out);
  and and_6 (and_6_out, l13, not_3_out);
  or or_1 (alu_src, not_5_out, not_6_out);
  or or_2 (alu_ctrl2, and_1_out, and_2_out, and_3_out, and_4_out);
  or or_3 (alu_ctrl1, and_5_out, not_2_out);
  or or_4 (alu_ctrl0, not_1_out, not_6_out, and_6_out);

  assign alu_ctrl3 = 1'b0;
endmodule

module OneBitAdder (
  input  A,
  input  B,
  input  C_in,
  output S,
  output C_out
);

  wire and_1_out, and_2_out, xor_1_out;

  xor xor_1 (xor_1_out, A, B);
  xor xor_2 (S, xor_1_out, C_in);
  and and_1 (and_1_out, xor_1_out, C_in);
  and and_2 (and_2_out, A, B);
  or or_1 (C_out, and_1_out, and_2_out);
endmodule

module OneBitAlu (
  input  [3:0] ALU_Ctrl,
  input  A,
  input  B,
  input  C_in,
  output R,
  output C_out
);

  wire and_1_out, multiplexer_1_out, not_1_out, onebitadder_1_s, or_1_out, xor_1_out;

  Multiplexer #(.enable("false")) multiplexer_1 (.in0(B), .in1(not_1_out), .out(multiplexer_1_out), .sel(ALU_Ctrl[2]));
  not not_1 (not_1_out, B);
  and and_1 (and_1_out, A, multiplexer_1_out);
  or or_1 (or_1_out, A, multiplexer_1_out);
  xor xor_1 (xor_1_out, A, multiplexer_1_out);
  OneBitAdder onebitadder_1 (.A(A), .B(multiplexer_1_out), .C_in(C_in), .S(onebitadder_1_s), .C_out(C_out));
  Multiplexer #(.enable("false"), .select(2)) multiplexer_2 (
    .in0(and_1_out), .in1(or_1_out), .in2(xor_1_out), .in3(onebitadder_1_s), .out(R), .sel(ALU_Ctrl[1:0]));
endmodule

module FourBitAlu (
  input  [3:0] ALU_ctrl,
  input  [3:0] A,
  input  [3:0] B,
  input  C_in,
  output [3:0] R,
  output C_out
);

  wire onebitalu_1_c_out, onebitalu_2_c_out, onebitalu_3_c_out;

  OneBitAlu onebitalu_1 (.ALU_Ctrl(ALU_ctrl), .A(A[0]), .B(B[0]), .C_in(C_in), .R(R[0]), .C_out(onebitalu_1_c_out));
  OneBitAlu onebitalu_2 (
    .ALU_Ctrl(ALU_ctrl), .A(A[1]), .B(B[1]), .C_in(onebitalu_1_c_out), .R(R[1]), .C_out(onebitalu_2_c_out));
  OneBitAlu onebitalu_3 (
    .ALU_Ctrl(ALU_ctrl), .A(A[2]), .B(B[2]), .C_in(onebitalu_2_c_out), .R(R[2]), .C_out(onebitalu_3_c_out));
  OneBitAlu onebitalu_4 (.ALU_Ctrl(ALU_ctrl), .A(A[3]), .B(B[3]), .C_in(onebitalu_3_c_out), .R(R[3]), .C_out(C_out));
endmodule

module ThirtyTwoBitAlu (
  input  [3:0] ALU_ctrl,
  input  [31:0] A,
  input  [31:0] B,
  output [31:0] Result,
  output C_out
);

  wire fourbitalu_1_c_out, fourbitalu_2_c_out, fourbitalu_3_c_out, fourbitalu_4_c_out, fourbitalu_5_c_out,
       fourbitalu_6_c_out, fourbitalu_7_c_out;

  FourBitAlu fourbitalu_1 (
    .ALU_ctrl(ALU_ctrl), .A(A[3:0]), .B(B[3:0]), .C_in(ALU_ctrl[2]), .R(Result[3:0]),
    .C_out(fourbitalu_1_c_out));
  FourBitAlu fourbitalu_2 (
    .ALU_ctrl(ALU_ctrl), .A(A[7:4]), .B(B[7:4]), .C_in(fourbitalu_1_c_out), .R(Result[7:4]),
    .C_out(fourbitalu_2_c_out));
  FourBitAlu fourbitalu_3 (
    .ALU_ctrl(ALU_ctrl), .A(A[11:8]), .B(B[11:8]), .C_in(fourbitalu_2_c_out), .R(Result[11:8]),
    .C_out(fourbitalu_3_c_out));
  FourBitAlu fourbitalu_4 (
    .ALU_ctrl(ALU_ctrl), .A(A[15:12]), .B(B[15:12]), .C_in(fourbitalu_3_c_out), .R(Result[15:12]),
    .C_out(fourbitalu_4_c_out));
  FourBitAlu fourbitalu_5 (
    .ALU_ctrl(ALU_ctrl), .A(A[19:16]), .B(B[19:16]), .C_in(fourbitalu_4_c_out), .R(Result[19:16]),
    .C_out(fourbitalu_5_c_out));
  FourBitAlu fourbitalu_6 (
    .ALU_ctrl(ALU_ctrl), .A(A[23:20]), .B(B[23:20]), .C_in(fourbitalu_5_c_out), .R(Result[23:20]),
    .C_out(fourbitalu_6_c_out));
  FourBitAlu fourbitalu_7 (
    .ALU_ctrl(ALU_ctrl), .A(A[27:24]), .B(B[27:24]), .C_in(fourbitalu_6_c_out), .R(Result[27:24]),
    .C_out(fourbitalu_7_c_out));
  FourBitAlu fourbitalu_8 (
    .ALU_ctrl(ALU_ctrl), .A(A[31:28]), .B(B[31:28]), .C_in(fourbitalu_7_c_out), .R(Result[31:28]),
    .C_out(C_out));
endmodule

module RegisterFour32 (
  input  [1:0] RReg1,
  input  [1:0] RReg2,
  input  [31:0] WData,
  input  Clock_in,
  input  Write,
  input  [1:0] WReg,
  output [31:0] RData1,
  output [31:0] RData2
);

  wire demultiplexer_1_out0, demultiplexer_1_out1, demultiplexer_1_out2, demultiplexer_1_out3;
  wire [31:0] register_1_q, register_2_q, register_3_q, register_4_q;

  Demultiplexer #(.enable("false"), .select(2)) demultiplexer_1 (
    .out0(demultiplexer_1_out0), .out1(demultiplexer_1_out1), .out2(demultiplexer_1_out2),
    .out3(demultiplexer_1_out3), .in(Write), .sel(WReg));
  Register #(.width(32)) register_1 (
    .D(WData), .en(demultiplexer_1_out0), .clk(Clock_in), .Q(register_1_q), .clr(Write));
  Register #(.width(32)) register_2 (
    .D(WData), .en(demultiplexer_1_out1), .clk(Clock_in), .Q(register_2_q));  // open: clr
  Register #(.width(32)) register_3 (
    .D(WData), .en(demultiplexer_1_out2), .clk(Clock_in), .Q(register_3_q));  // open: clr
  Register #(.width(32)) register_4 (
    .D(WData), .en(demultiplexer_1_out3), .clk(Clock_in), .Q(register_4_q));  // open: clr
  Multiplexer #(.enable("false"), .select(2), .width(32)) multiplexer_1 (
    .in0(register_1_q), .in1(register_2_q), .in2(register_3_q), .in3(register_4_q), .out(RData1), .sel(RReg1));
  Multiplexer #(.enable("false"), .select(2), .width(32)) multiplexer_2 (
    .in0(register_1_q), .in1(register_2_q), .in2(register_3_q), .in3(register_4_q), .out(RData2), .sel(RReg2));
endmodule

module RegisterFile (
  input  [4:0] RReg1,
  input  [4:0] RReg2,
  input  [31:0] WData,
  input  Clock_in,
  input  Write,
  input  [4:0] WReg,
  output [31:0] RData1,
  output [31:0] RData2
);

  wire W3_0, W7_4, W11_8, W15_12, W19_16, W23_20, W27_24, W31_28;
  wire [31:0] registerfour32_1_rdata1, registerfour32_1_rdata2, registerfour32_2_rdata1,
       registerfour32_2_rdata2, registerfour32_3_rdata1, registerfour32_3_rdata2, registerfour32_4_rdata1,
       registerfour32_4_rdata2, registerfour32_5_rdata1, registerfour32_5_rdata2, registerfour32_6_rdata1,
       registerfour32_6_rdata2, registerfour32_7_rdata1, registerfour32_7_rdata2, registerfour32_8_rdata1,
       registerfour32_8_rdata2;

  Demultiplexer #(.enable("false"), .select(3)) demultiplexer_1 (
    .out0(W3_0), .out1(W7_4), .out2(W11_8), .out3(W15_12), .out4(W19_16), .out5(W23_20), .out6(W27_24),
    .out7(W31_28), .in(Write), .sel(WReg[4:2]));
  RegisterFour32 registerfour32_1 (
    .RReg1(RReg1[1:0]), .RReg2(RReg2[1:0]), .WData(WData), .Clock_in(Clock_in), .Write(W3_0),
    .WReg(RReg1[1:0]), .RData1(registerfour32_1_rdata1), .RData2(registerfour32_1_rdata2));
  RegisterFour32 registerfour32_2 (
    .RReg1(RReg1[1:0]), .RReg2(RReg2[1:0]), .WData(WData), .Clock_in(Clock_in), .Write(W7_4),
    .WReg(RReg1[1:0]), .RData1(registerfour32_2_rdata1), .RData2(registerfour32_2_rdata2));
  RegisterFour32 registerfour32_3 (
    .RReg1(RReg1[1:0]), .RReg2(RReg2[1:0]), .WData(WData), .Clock_in(Clock_in), .Write(W11_8),
    .WReg(RReg1[1:0]), .RData1(registerfour32_3_rdata1), .RData2(registerfour32_3_rdata2));
  RegisterFour32 registerfour32_4 (
    .RReg1(RReg1[1:0]), .RReg2(RReg2[1:0]), .WData(WData), .Clock_in(Clock_in), .Write(W15_12),
    .RData1(registerfour32_4_rdata1), .RData2(registerfour32_4_rdata2));  // open: WReg
  RegisterFour32 registerfour32_5 (
    .RReg1(RReg1[1:0]), .RReg2(RReg2[1:0]), .WData(WData), .Clock_in(Clock_in), .Write(W19_16),
    .WReg(RReg1[1:0]), .RData1(registerfour32_5_rdata1), .RData2(registerfour32_5_rdata2));
  RegisterFour32 registerfour32_6 (
    .RReg1(RReg1[1:0]), .RReg2(RReg2[1:0]), .WData(WData), .Clock_in(Clock_in), .Write(W23_20),
    .WReg(RReg1[1:0]), .RData1(registerfour32_6_rdata1), .RData2(registerfour32_6_rdata2));
  RegisterFour32 registerfour32_7 (
    .RReg1(RReg1[1:0]), .RReg2(RReg2[1:0]), .WData(WData), .Clock_in(Clock_in), .Write(W27_24),
    .WReg(RReg1[1:0]), .RData1(registerfour32_7_rdata1), .RData2(registerfour32_7_rdata2));
  RegisterFour32 registerfour32_8 (
    .RReg1(RReg1[1:0]), .RReg2(RReg2[1:0]), .WData(WData), .Clock_in(Clock_in), .Write(W31_28),
    .WReg(RReg1[1:0]), .RData1(registerfour32_8_rdata1), .RData2(registerfour32_8_rdata2));
  Multiplexer #(.enable("false"), .select(3), .width(32)) multiplexer_1 (
    .in0(registerfour32_1_rdata1), .in1(registerfour32_2_rdata1), .in2(registerfour32_3_rdata1),
    .in3(registerfour32_4_rdata1), .in4(registerfour32_5_rdata1), .in5(registerfour32_6_rdata1),
    .in6(registerfour32_7_rdata1), .in7(registerfour32_8_rdata1), .out(RData1), .sel(RReg1[4:2]));
  Multiplexer #(.enable("false"), .select(3), .width(32)) multiplexer_2 (
    .in0(registerfour32_1_rdata2), .in1(registerfour32_2_rdata2), .in2(registerfour32_3_rdata2),
    .in3(registerfour32_4_rdata2), .in4(registerfour32_5_rdata2), .in5(registerfour32_6_rdata2),
    .in6(registerfour32_7_rdata2), .in7(registerfour32_8_rdata2), .out(RData2), .sel(RReg2[4:2]));

  assign WReg[1:0] = RReg1[1:0];
endmodule

module RegisterFileLong (
  input  [4:0] RReg1,
  input  [4:0] RReg2,
  input  [31:0] WData,
  input  Clock_in,
  input  Write,
  input  [4:0] WReg,
  output [31:0] RData1,
  output [31:0] RData2
);

  wire demultiplexer_1_out0, demultiplexer_1_out1, demultiplexer_1_out2, demultiplexer_1_out3,
       demultiplexer_1_out4, demultiplexer_1_out5, demultiplexer_1_out6, demultiplexer_1_out7,
       demultiplexer_1_out8, demultiplexer_1_out9, demultiplexer_1_out10, demultiplexer_1_out11,
       demultiplexer_1_out12, demultiplexer_1_out13, demultiplexer_1_out14, demultiplexer_1_out15,
       demultiplexer_1_out16, demultiplexer_1_out17, demultiplexer_1_out18, demultiplexer_1_out19,
       demultiplexer_1_out20, demultiplexer_1_out21, demultiplexer_1_out22, demultiplexer_1_out23, r24, r25,
       r26, r27, r28, r29, r30, r31;
  wire [31:0] q0, q1, q2, q3, q4, q5, q6, q7, q8, q9, q10, q11, q12, q13, q14, q15, q16, q17, q18, q19, q20,
       q21, q22, q23, q24, q25, q26, q27, q28, q29, q30, q31;

  Demultiplexer #(.enable("false"), .select(5)) demultiplexer_1 (
    .out0(demultiplexer_1_out0), .out1(demultiplexer_1_out1), .out2(demultiplexer_1_out2),
    .out3(demultiplexer_1_out3), .out4(demultiplexer_1_out4), .out5(demultiplexer_1_out5),
    .out6(demultiplexer_1_out6), .out7(demultiplexer_1_out7), .out8(demultiplexer_1_out8),
    .out9(demultiplexer_1_out9), .out10(demultiplexer_1_out10), .out11(demultiplexer_1_out11),
    .out12(demultiplexer_1_out12), .out13(demultiplexer_1_out13), .out14(demultiplexer_1_out14),
    .out15(demultiplexer_1_out15), .out16(demultiplexer_1_out16), .out17(demultiplexer_1_out17),
    .out18(demultiplexer_1_out18), .out19(demultiplexer_1_out19), .out20(demultiplexer_1_out20),
    .out21(demultiplexer_1_out21), .out22(demultiplexer_1_out22), .out23(demultiplexer_1_out23), .out24(r24),
    .out25(r25), .out26(r26), .out27(r27), .out28(r28), .out29(r29), .out30(r30), .out31(r31), .in(Write),
    .sel(WReg));
  Register #(.width(32)) register_1 (.D(WData), .en(demultiplexer_1_out0), .clk(Clock_in), .Q(q0), .clr(Write));
  Register #(.width(32)) register_2 (.D(WData), .en(demultiplexer_1_out1), .clk(Clock_in), .Q(q1));  // open: clr
  Register #(.width(32)) register_3 (.D(WData), .en(demultiplexer_1_out2), .clk(Clock_in), .Q(q2));  // open: clr
  Register #(.width(32)) register_4 (.D(WData), .en(demultiplexer_1_out3), .clk(Clock_in), .Q(q3));  // open: clr
  Register #(.width(32)) register_5 (.D(WData), .en(demultiplexer_1_out4), .clk(Clock_in), .Q(q4));  // open: clr
  Register #(.width(32)) register_6 (.D(WData), .en(demultiplexer_1_out5), .clk(Clock_in), .Q(q5));  // open: clr
  Register #(.width(32)) register_7 (.D(WData), .en(demultiplexer_1_out6), .clk(Clock_in), .Q(q6));  // open: clr
  Register #(.width(32)) register_8 (.D(WData), .en(demultiplexer_1_out7), .clk(Clock_in), .Q(q7));  // open: clr
  Register #(.width(32)) register_9 (.D(WData), .en(demultiplexer_1_out8), .clk(Clock_in), .Q(q8));  // open: clr
  Register #(.width(32)) register_10 (.D(WData), .en(demultiplexer_1_out9), .clk(Clock_in), .Q(q9));  // open: clr
  Register #(.width(32)) register_11 (.D(WData), .en(demultiplexer_1_out10), .clk(Clock_in), .Q(q10));  // open: clr
  Register #(.width(32)) register_12 (.D(WData), .en(demultiplexer_1_out11), .clk(Clock_in), .Q(q11));  // open: clr
  Register #(.width(32)) register_13 (.D(WData), .en(demultiplexer_1_out12), .clk(Clock_in), .Q(q12));  // open: clr
  Register #(.width(32)) register_14 (.D(WData), .en(demultiplexer_1_out13), .clk(Clock_in), .Q(q13));  // open: clr
  Register #(.width(32)) register_15 (.D(WData), .en(demultiplexer_1_out14), .clk(Clock_in), .Q(q14));  // open: clr
  Register #(.width(32)) register_16 (.D(WData), .en(demultiplexer_1_out15), .clk(Clock_in), .Q(q15));  // open: clr
  Register #(.width(32)) register_17 (.D(WData), .en(demultiplexer_1_out16), .clk(Clock_in), .Q(q16));  // open: clr
  Register #(.width(32)) register_18 (.D(WData), .en(demultiplexer_1_out17), .clk(Clock_in), .Q(q17));  // open: clr
  Register #(.width(32)) register_19 (.D(WData), .en(demultiplexer_1_out18), .clk(Clock_in), .Q(q18));  // open: clr
  Register #(.width(32)) register_20 (.D(WData), .en(demultiplexer_1_out19), .clk(Clock_in), .Q(q19));  // open: clr
  Register #(.width(32)) register_21 (.D(WData), .en(demultiplexer_1_out20), .clk(Clock_in), .Q(q20));  // open: clr
  Register #(.width(32)) register_22 (.D(WData), .en(demultiplexer_1_out21), .clk(Clock_in), .Q(q21));  // open: clr
  Register #(.width(32)) register_23 (.D(WData), .en(demultiplexer_1_out22), .clk(Clock_in), .Q(q22));  // open: clr
  Register #(.width(32)) register_24 (.D(WData), .en(demultiplexer_1_out23), .clk(Clock_in), .Q(q23));  // open: clr
  Register #(.width(32)) register_25 (.D(WData), .en(r24), .clk(Clock_in), .Q(q24));  // open: clr
  Register #(.width(32)) register_26 (.D(WData), .en(r25), .clk(Clock_in), .Q(q25));  // open: clr
  Register #(.width(32)) register_27 (.D(WData), .en(r26), .clk(Clock_in), .Q(q26));  // open: clr
  Register #(.width(32)) register_28 (.D(WData), .en(r27), .clk(Clock_in), .Q(q27));  // open: clr
  Register #(.width(32)) register_29 (.D(WData), .en(r28), .clk(Clock_in), .Q(q28));  // open: clr
  Register #(.width(32)) register_30 (.D(WData), .en(r29), .clk(Clock_in), .Q(q29));  // open: clr
  Register #(.width(32)) register_31 (.D(WData), .en(r30), .clk(Clock_in), .Q(q30));  // open: clr
  Register #(.width(32)) register_32 (.D(WData), .en(r31), .clk(Clock_in), .Q(q31));  // open: clr
  Multiplexer #(.enable("false"), .select(5), .width(32)) multiplexer_1 (
    .in0(q0), .in1(q1), .in2(q2), .in3(q3), .in4(q4), .in5(q5), .in6(q6), .in7(q7), .in8(q8), .in9(q9),
    .in10(q10), .in11(q11), .in12(q12), .in13(q13), .in14(q14), .in15(q15), .in16(q16), .in17(q17),
    .in18(q18), .in19(q19), .in20(q20), .in21(q21), .in22(q22), .in23(q23), .in24(q24), .in25(q25),
    .in26(q26), .in27(q27), .in28(q28), .in29(q29), .in30(q30), .in31(q31), .out(RData1), .sel(RReg1));
  Multiplexer #(.enable("false"), .select(5), .width(32)) multiplexer_2 (
    .in0(q0), .in1(q1), .in2(q2), .in3(q3), .in4(q4), .in5(q5), .in6(q6), .in7(q7), .in8(q8), .in9(q9),
    .in10(q10), .in11(q11), .in12(q12), .in13(q13), .in14(q14), .in15(q15), .in16(q16), .in17(q17),
    .in18(q18), .in19(q19), .in20(q20), .in21(q21), .in22(q22), .in23(q23), .in24(q24), .in25(q25),
    .in26(q26), .in27(q27), .in28(q28), .in29(q29), .in30(q30), .in31(q31), .out(RData2), .sel(RReg2));
endmodule
